// Logisim project 6502.circ as structural Verilog: 5 circuits, main circuit main
module main (
);

  wire clock_1_out, clock_generator_1_phi1, clock_generator_1_phi2;

  Clock clock_1 (.out(clock_1_out));
  Clock_Generator clock_generator_1 (.clk0(clock_1_out), .phi1(clock_generator_1_phi1), .phi2(clock_generator_1_phi2));
endmodule

module _6502 (
  input  ADL_ABL,
  input  _0_ADL0,
  input  _0_ADL1,
  input  _0_ADL2,
  input  YSB,
  input  SBY,
  input  XSB,
  input  SBX,
  input  SSB,
  input  SADL,
  input  SBS,
  input  SS,
  input  phi1,
  input  phi2,
  input  in_15,
  input  in_16,
  input  in_17,
  input  [7:0] in_18,
  input  in_19,
  input  in_20,
  input  in_21,
  output [7:0] out_22,
  output [7:0] out_23,
  output [7:0] out_24,
  output [15:0] out_25
);

  wire and_1_out, and_2_out;
  wire [2:0] and_3_out;
  wire [7:0] AC_q, controlled_buffer_8_out, DOR_q, IDL_q, PCH_q, PCL_q, S_q, undriven, X_q, Y_q;

  and and_1 (and_1_out, phi1, ADL_ABL);
  buf and_2 (and_2_out, phi1);  // AND_Gate
  and and_3 (and_3_out[0], ~_0_ADL0, out_24[0]);  // AND_Gate
  and and_4 (and_3_out[1], ~_0_ADL1, out_24[1]);  // AND_Gate
  and and_5 (and_3_out[2], ~_0_ADL2, out_24[2]);  // AND_Gate
  Register #(.trigger("high")) ABL (
    .D({out_24[7:3], and_3_out}), .en(and_1_out), .Q(out_25[7:0]), .clk(and_1_out));  // open: clr
  Register #(.trigger("high")) ABH (
    .D(controlled_buffer_8_out), .en(and_2_out), .Q(out_25[15:8]), .clk(and_2_out));  // open: clr
  assign out_22 = YSB ? Y_q : 8'bz;  // Controlled_Buffer controlled_buffer_1
  Register #(.trigger("high")) Y (.D(out_22), .en(SBY), .Q(Y_q), .clk(SBY));  // open: clr
  assign out_22 = XSB ? X_q : 8'bz;  // Controlled_Buffer controlled_buffer_2
  Register #(.trigger("high")) X (.D(out_22), .en(SBX), .Q(X_q), .clk(SBX));  // open: clr
  assign out_22 = SSB ? S_q : 8'bz;  // Controlled_Buffer controlled_buffer_3
  Register #(.trigger("high")) S (.D(out_22), .en(SBS), .Q(S_q), .clk(SBS));  // open: clr
  assign out_24 = SADL ? S_q : 8'bz;  // Controlled_Buffer controlled_buffer_4
  Register #(.trigger("high")) ALUA ();  // open: D, en, Q, clk, clr
  Register #(.trigger("high")) ALUB ();  // open: D, en, Q, clk, clr
  Register #(.trigger("high")) ALU ();  // open: D, en, Q, clk, clr
  assign out_22 = in_16 ? AC_q : 8'bz;  // Controlled_Buffer controlled_buffer_5
  Register #(.trigger("high")) AC (.D(out_22), .Q(AC_q));  // open: en, clk, clr
  assign out_24 = in_17 ? PCL_q : 8'bz;  // Controlled_Buffer controlled_buffer_6
  Register #(.trigger("high")) PCHP ();  // open: D, en, Q, clk, clr
  Register #(.trigger("high")) PCLP ();  // open: D, en, Q, clk, clr
  Register #(.trigger("high")) PCL (.Q(PCL_q));  // open: D, en, clk, clr
  Register #(.trigger("high")) PCH (.Q(PCH_q));  // open: D, en, clk, clr
  assign out_24 = in_19 ? IDL_q : 8'bz;  // Controlled_Buffer controlled_buffer_7
  assign controlled_buffer_8_out = in_20 ? PCH_q : 8'bz;  // Controlled_Buffer controlled_buffer_8
  assign controlled_buffer_8_out = in_21 ? IDL_q : 8'bz;  // Controlled_Buffer controlled_buffer_9
  Register #(.trigger("high")) DOR (.D(undriven), .Q(DOR_q));  // open: en, clk, clr
  Register #(.trigger("high")) IDL (.D(in_18), .Q(IDL_q));  // open: en, clk, clr
  assign out_23 = in_15 ? DOR_q : 8'bz;  // Controlled_Buffer controlled_buffer_10
endmodule

module Clock_Generator (
  input  clk0,
  output phi1,
  output phi2
);

  not not_1 (phi1, clk0);

  assign phi2 = clk0;
endmodule

module PLA (
  input  nIRQP,
  input  t5,
  input  t4,
  input  t3,
  input  t2,
  input  [7:0] IR,
  input  clock1,
  input  clock2,
  output op_sty_cpy_mem,
  output op_T3_ind_y,
  output op_T2_abs_y,
  output op_T0_iny_dey,
  output x_op_T0_tya,
  output op_T0_cpy_iny,
  output op_T2_idx_x_xy,
  output op_xy,
  output op_T2_ind_x,
  output x_op_T0_txa,
  output op_T0_dex,
  output op_T0_cpx_inx,
  output op_from_x,
  output op_T0_txs,
  output op_T0_ldx_tax_tsx,
  output op_T__dex,
  output op_T__inx,
  output op_T0_tsx,
  output op_T__iny_dey,
  output op_T0_ldy_mem,
  output op_T0_tay_ldy_not_idx,
  output nIRQP_2,
  output op_T0_jsr,
  output op_T5_brk,
  output op_T0_php_pha,
  output op_T4_rts,
  output op_T3_plp_pla,
  output op_T5_rti,
  output op_ror,
  output op_T2,
  output op_T0_eor,
  output op_jmp,
  output op_T2_abs,
  output op_T0_ora,
  output op_T2_ADL_ADD,
  output op_T0,
  output op_T2_stack,
  output op_T3_stack_bit_jmp,
  output op_T4_brk_jsr,
  output op_T4_rti,
  output op_T3_ind_x,
  output op_T4_ind_y,
  output op_T2_ind_y,
  output op_T3_abs_idx,
  output op_plp_pla,
  output op_inc_nop,
  output op_T4_ind_x,
  output x_op_T3_ind_y,
  output op_rti_rts
);

  wire nor_47_out;

  nor nor_1 (op_sty_cpy_mem, IR[6], ~IR[2], ~IR[7], IR[5], nor_47_out);  // NOR_Gate
  nor nor_2 (op_T3_ind_y, ~IR[4], ~IR[0], t3, IR[3], IR[2]);  // NOR_Gate
  nor nor_3 (op_T2_abs_y, ~IR[4], ~IR[0], t2, ~IR[3], IR[2]);  // NOR_Gate
  nor nor_4 (op_T0_iny_dey, clock1, IR[4], ~IR[7], ~IR[3], IR[5], nor_47_out, IR[2]);  // NOR_Gate
  nor nor_5 (x_op_T0_tya, clock1, IR[6], ~IR[7], ~IR[4], ~IR[3], IR[5], nor_47_out, IR[2]);  // NOR_Gate
  nor nor_6 (op_T0_cpy_iny, clock1, IR[4], ~IR[7], ~IR[6], IR[5], nor_47_out);  // NOR_Gate
  nor nor_7 (op_T2_idx_x_xy, ~IR[2], ~IR[4], t2);  // NOR_Gate
  nor nor_8 (op_xy, IR[6], ~IR[7], ~IR[1]);  // NOR_Gate
  nor nor_9 (op_T2_ind_x, IR[4], ~IR[0], t2, IR[3], IR[2]);  // NOR_Gate
  nor nor_10 (x_op_T0_txa, clock1, IR[6], IR[4], ~IR[7], ~IR[1], ~IR[3], IR[5], IR[2]);  // NOR_Gate
  nor nor_11 (op_T0_dex, clock1, IR[4], ~IR[7], ~IR[1], ~IR[6], ~IR[3], IR[5], IR[2]);  // NOR_Gate
  nor nor_12 (op_T0_cpx_inx, clock1, IR[4], ~IR[7], ~IR[6], nor_47_out, ~IR[5]);  // NOR_Gate
  nor nor_13 (op_from_x, IR[6], ~IR[7], ~IR[1], IR[5]);  // NOR_Gate
  nor nor_14 (op_T0_txs, clock1, IR[6], ~IR[7], ~IR[1], ~IR[4], ~IR[3], IR[5], IR[2]);  // NOR_Gate
  nor nor_15 (op_T0_ldx_tax_tsx, clock1, IR[6], ~IR[7], ~IR[1], ~IR[5]);  // NOR_Gate
  nor nor_16 (op_T__dex, IR[4], clock2, ~IR[7], ~IR[1], ~IR[6], ~IR[3], IR[5], IR[2]);  // NOR_Gate
  nor nor_17 (op_T__inx, IR[4], clock2, ~IR[7], ~IR[6], ~IR[3], nor_47_out, ~IR[5], IR[2]);  // NOR_Gate
  nor nor_18 (op_T0_tsx, clock1, IR[6], ~IR[7], ~IR[1], ~IR[4], ~IR[3], ~IR[5], IR[2]);  // NOR_Gate
  nor nor_19 (op_T__iny_dey, IR[4], clock2, ~IR[7], ~IR[3], IR[5], nor_47_out, IR[2]);  // NOR_Gate
  nor nor_20 (op_T0_ldy_mem, clock1, IR[6], ~IR[2], ~IR[7], nor_47_out, ~IR[5]);  // NOR_Gate
  nor nor_21 (op_T0_tay_ldy_not_idx, clock1, IR[6], IR[4], ~IR[7], nor_47_out, ~IR[5]);  // NOR_Gate
  nor nor_22 (op_T0_jsr, clock1, IR[6], IR[4], IR[7], IR[3], nor_47_out, ~IR[5], IR[2]);  // NOR_Gate
  nor nor_23 (op_T5_brk, IR[6], IR[4], IR[7], IR[3], IR[5], t5, nor_47_out, IR[2]);
  nor nor_24 (op_T0_php_pha, clock1, IR[4], IR[7], ~IR[3], IR[5], nor_47_out, IR[2]);  // NOR_Gate
  nor nor_25 (op_T4_rts, IR[4], IR[7], t4, ~IR[6], IR[3], nor_47_out, ~IR[5], IR[2]);  // NOR_Gate
  nor nor_26 (op_T3_plp_pla, IR[4], IR[7], t3, ~IR[3], nor_47_out, ~IR[5], IR[2]);  // NOR_Gate
  nor nor_27 (op_T5_rti, IR[4], IR[7], ~IR[6], IR[3], IR[5], t5, nor_47_out, IR[2]);  // NOR_Gate
  nor nor_28 (op_ror, IR[7], ~IR[1], ~IR[6], ~IR[4]);  // NOR_Gate
  nor nor_29 (op_T0_eor, clock1, IR[7], ~IR[0], ~IR[6], IR[5]);  // NOR_Gate
  not not_1 (op_T2, t2);
  // NOR_Gate nor_30 has open pins: out=op_jmp
  // NOR_Gate nor_31 has open pins: out=op_T2_abs
  // NOR_Gate nor_32 has open pins: out=op_T0_ora
  // NOR_Gate nor_33 has open pins: out=op_T2_ADL_ADD
  // NOT_Gate not_2 has open pins: in=open, out=op_T0
  // NOR_Gate nor_34 has open pins: out=op_T2_stack
  // NOR_Gate nor_35 has open pins: out=op_T3_stack_bit_jmp
  // NOR_Gate nor_36 has open pins: out=op_T4_brk_jsr
  // NOR_Gate nor_37 has open pins: out=op_T4_rti
  // NOR_Gate nor_38 has open pins: out=op_T3_ind_x
  // NOR_Gate nor_39 has open pins: out=op_T4_ind_y
  // NOR_Gate nor_40 has open pins: out=op_T2_ind_y
  // NOR_Gate nor_41 has open pins: out=op_T3_abs_idx
  // NOR_Gate nor_42 has open pins: out=op_plp_pla
  // NOR_Gate nor_43 has open pins: out=op_inc_nop
  // NOR_Gate nor_44 has open pins: out=op_T4_ind_x
  // NOR_Gate nor_45 has open pins: out=x_op_T3_ind_y
  // NOR_Gate nor_46 has open pins: out=op_rti_rts
  nor nor_47 (nor_47_out, IR[0], IR[1]);

  assign nIRQP_2 = nIRQP;
endmodule

module Random_Logic (
  input  op_sty_cpy_mem,
  input  op_T3_ind_y,
  input  op_T2_abs_y,
  input  op_T0_iny_dey,
  input  x_op_T0_tya,
  input  op_T0_cpy_iny,
  output ADL_ABL,
  output _0_ADL0,
  output _0_ADL1,
  output _0_ADL2,
  output YSB,
  output SBY,
  output XSB,
  output SBX,
  output SSB,
  output SADL,
  output SBS,
  output SS
);

  wire nor_2_out;

  // NOR_Gate nor_1 has open pins: out=ADL_ABL
  // NOT_Gate not_1 has open pins: in=open, out=_0_ADL0
  // NOT_Gate not_2 has open pins: in=open, out=_0_ADL1
  nor nor_2 (nor_2_out, op_T3_ind_y, op_T2_abs_y, op_T0_iny_dey, x_op_T0_tya, op_T0_cpy_iny);
endmodule
